# Fritzing sketch projeto-03 (saved by Fritzing 0.9.3b)
breadboards: 1

parts:
  LED1 = smd LED [color="Red (633nm)" package="1206 [SMD]"]
  Componente1 = Arduino Uno (Rev3)
  R2 = Resistor [tolerance=±5% resistance=220 package="0603 [SMD]"]
  R3 = Resistor [tolerance=±5% resistance=220 package="0603 [SMD]"]
  R4 = Resistor [tolerance=±5% resistance=220 package="0603 [SMD]"]
  LED2 = smd LED [color="Yellow (595nm)" package="1206 [SMD]"]
  LED3 = smd LED [color="Blue (525nm)" package="1206 [SMD]"]

nets:
  N1: LED1.anode, R2.Pin_0
  N2: Componente1.D11_PWM/MOSI, R4.Pin_1
  N3: Componente1.D12/MISO, R3.Pin_1
  N4: Componente1.D13/SCK, R2.Pin_1
  N5: Componente1.GND, LED2.cathode, LED3.cathode
  N6: R3.Pin_0, LED2.anode
  N7: R4.Pin_0, LED3.anode
