# Fritzing sketch projeto-04 (saved by Fritzing 0.9.3b)
breadboards: 1

parts:
  Componente1 = Arduino Uno (Rev3)
  R1 = Resistor [tolerance=±5% resistance=220 package=THT]
  LED1 = smd LED [color="Red (633nm)" package="0603 [SMD]"]
  U1 = 4ChannelRelay
  Componente2 = RFID-RC522 [part_number=101218]

nets:
  N1: Componente1.D9_PWM, Componente2.RST
  N2: Componente1.D10_PWM/SS, Componente2.SDA
  N3: Componente1.D11_PWM/MOSI, Componente2.MOSI
  N4: Componente1.D12/MISO, Componente2.MISO
  N5: Componente1.D13/SCK, Componente2.SCK
  N6: Componente1.D4, U1.connector5
  N7: Componente1.D7, U1.connector2
  3V3: Componente1.3V3, Componente2.3.3V
  N8: Componente1.5V, U1.connector0
  GND: Componente1.GND, LED1.cathode, U1.connector1, Componente2.GND
  N9: R1.Pin_0, U1.connector6
  N10: R1.Pin_1, LED1.anode
