# Fritzing sketch projeto-05 (saved by Fritzing 0.9.3b)
breadboards: 1

parts:
  Componente1 = Arduino Uno (Rev3)
  DHT2 = DHT11 Humitidy and Temperature Sensor

nets:
  N1: Componente1.A0, DHT2.DATA
  5V: Componente1.5V, DHT2.VDD
  GND: Componente1.GND, DHT2.GND

custom parts:
  DHT11 Humitidy and Temperature Sensor: DHT11 Humidity and Temperature Sensor
